# Fritzing sketch Ultimatrix_fritzing_design (saved by Fritzing 1.0.4)

parts:
  DFRobot_DFPlayer_Mini1 = DFRobot DFPlayer Mini [part_number=DFR0299]
  Grove1 = Grove OLED 128x96
  CPU1 = NodeMCU WROOM ESP 32
  U1 = POT [knob_status=50% power=0.5W package=pot_alpha_rv16af-20]
  S3 = Round Pushbutton
  S4 = Round Pushbutton
  S5 = Round Pushbutton
  S6 = Round Pushbutton
  U2 = LIPO-2000mAh [package=lipo-2000]
  SP1 = SPEAKER [package=pcb_mount_speaker]
  R1 = Resistor [tolerance=±5% power=0.25W resistance=220 package=THT]
  R2 = Resistor [tolerance=±5% power=0.25W resistance=220 package=THT]

nets:
  N1: DFRobot_DFPlayer_Mini1.VCC, CPU1.pin_17, U1.A
  N2: DFRobot_DFPlayer_Mini1.SPK_1, SP1.+
  N3: DFRobot_DFPlayer_Mini1.GND-1, CPU1.pin_18
  N4: DFRobot_DFPlayer_Mini1.SPK_2, SP1.-
  N5: Grove1.GND, CPU1.pin_15, U1.E, S3.leg0, S4.leg0, S5.leg0, S6.leg0, U2.-
  N6: Grove1.VCC, CPU1.pin_16, U2.+
  N7: Grove1.SDA, CPU1.pin_27
  N8: Grove1.SCL, CPU1.pin_30
  N9: CPU1.pin_5, U1.S
  N10: CPU1.pin_7, S4.leg1
  N11: CPU1.pin_8, S6.leg1
  N12: CPU1.pin_9, S5.leg1
  N13: CPU1.pin_10, S3.leg1
  N14: CPU1.pin_22, R2.Pin_0
  N15: CPU1.pin_23, R1.Pin_0

notes:
  OLED 128X128
  PLAY/PAUSE
  SELECTOR
  VOL+
  VOL-
  MODE
  DFPLAYER
  SPEAKER
  ESP32 30 PINS
  LIPO BATTERY

custom parts:
  NodeMCU WROOM ESP 32: 30 pol Development Kit
